# Fritzing sketch monitor agua (saved by Fritzing 0.9.3b)
breadboards: 1

parts:
  VALVE1 = Plastic Solenoid Valve
  VALVE2 = Plastic Solenoid Valve
  Mod1 = TTGO-T-Call-V1.3-ESP32 [package=THT]
  U1 = RELAY [package=relay-jzc]
  U2 = RELAY [package=relay-jzc]
  LED1 = LEDs [package=led10mm]
  M1 = water level switch
  J1 = 120V duplex outlet_1  # not connected
  R1 = Resistor [tolerance=±5% resistance=220 package="0805 [SMD]"]
  LED2 = LEDs [package=led10mm]
  R2 = Resistor [tolerance=±5% resistance=220 package="0805 [SMD]"]
  R3 = Resistor [tolerance=±5% resistance=10k package="0805 [SMD]"]

nets:
  N1: VALVE1.no_name_yet#2, U1.MAIN
  N2: VALVE2.no_name_yet#2, U2.MAIN
  N3: Mod1.34, R3.Pin_1
  N4: Mod1.25, R1.Pin_1
  N5: Mod1.26, R2.Pin_1
  N6: Mod1.GND, U1.NC
  N7: Mod1.5V, U1.COIL2, M1.pin2
  N8: U1.NO, LED2.C
  N9: U2.NO, LED1.C
  N10: LED1.A, R1.Pin_0
  N11: M1.pin1, R3.Pin_0
  N12: LED2.A, R2.Pin_0

custom parts:
  TTGO-T-Call-V1.3-ESP32: LILYGO® TTGO T-Call V1.3 ESP32 Wireless Module GPRS Antenna SIM Card SIM800L Module
  water level switch: Generic water level float switch.
  120V duplex outlet_1: 120V duplex outlet.
